// Logisim project CA_final_circuit.circ as structural Verilog: 1 circuit, main circuit main
module main (
  input  [4:0] A,
  input  [4:0] B,
  output [5:0] out_3,
  output [5:0] out_4,
  output [8:0] out_5
);

  wire comparator_1_eq, comparator_1_gt, comparator_2_eq, comparator_2_gt, xor_1_out, xor_2_out, xor_3_out;
  wire [2:0] and_2_out;
  wire [3:0] adder_1_out, adder_2_out, adder_3_out, and_5_out, and_9_out, and_13_out;
  wire [3:1] adder_4_out;
  wire [3:3] adder_4_cout;
  wire [4:0] subtractor_1_out, subtractor_2_out, subtractor_3_out;
  wire [4:4] adder_1_cout, adder_2_cout;
  wire [5:0] multiplexer_3_out, multiplexer_5_out, multiplexer_6_out, multiplexer_7_out, subtractor_4_out;

  xor xor_1 (xor_1_out, A[4], B[4]);
  Multiplexer multiplexer_1 (.in0(1'b0), .in1(1'b1), .out(out_5[8]), .sel(xor_1_out));  // open: en
  not not_1 (subtractor_4_out[5], B[4]);
  and and_1 (out_5[0], B[0], A[0]);
  and and_2 (and_2_out[0], B[0], A[1]);
  and and_3 (and_2_out[1], B[0], A[2]);
  and and_4 (and_2_out[2], B[0], A[3]);
  and and_5 (and_5_out[0], B[1], A[0]);
  and and_6 (and_5_out[1], B[1], A[1]);
  and and_7 (and_5_out[2], B[1], A[2]);
  and and_8 (and_5_out[3], B[1], A[3]);
  and and_9 (and_9_out[0], B[2], A[0]);
  and and_10 (and_9_out[1], B[2], A[1]);
  and and_11 (and_9_out[2], B[2], A[2]);
  and and_12 (and_9_out[3], B[2], A[3]);
  and and_13 (and_13_out[0], B[3], A[0]);
  and and_14 (and_13_out[1], B[3], A[1]);
  and and_15 (and_13_out[2], B[3], A[2]);
  and and_16 (and_13_out[3], B[3], A[3]);
  xor xor_2 (xor_2_out, A[4], B[4]);
  Comparator #(.width(4), .mode("unsigned")) comparator_1 (
    .a(A[3:0]), .b(B[3:0]), .gt(comparator_1_gt), .eq(comparator_1_eq));  // open: lt
  Adder #(.width(4)) adder_1 (.a(A[3:0]), .b(B[3:0]), .out(adder_1_out), .cout(adder_1_cout[4]));  // open: cin
  Adder #(.width(4)) adder_2 (.a(A[3:0]), .b(B[3:0]), .out(adder_2_out), .cout(adder_2_cout[4]));  // open: cin
  xor xor_3 (xor_3_out, A[4], subtractor_4_out[5]);
  Comparator #(.width(4), .mode("unsigned")) comparator_2 (
    .a(A[3:0]), .b(B[3:0]), .gt(comparator_2_gt), .eq(comparator_2_eq));  // open: lt
  Adder #(.width(4)) adder_3 (
    .a({1'b0, and_2_out}), .b(and_5_out), .out({adder_3_out[2:0], out_5[1]}), .cout(adder_3_out[3]));  // open: cin
  Adder #(.width(4)) adder_4 (
    .a(adder_3_out), .b(and_9_out), .out({adder_4_out, out_5[2]}), .cout(adder_4_cout[3]));  // open: cin
  Adder #(.width(4)) adder_5 (
    .a({adder_4_cout[3], adder_4_out}), .b(and_13_out), .out(out_5[6:3]), .cout(out_5[7]));  // open: cin
  Subtractor #(.width(4)) subtractor_1 (
    .a(A[3:0]), .b(B[3:0]), .out(subtractor_1_out[3:0]), .bout(subtractor_1_out[4]));  // open: bin
  Subtractor #(.width(4)) subtractor_2 (
    .a(B[3:0]), .b(A[3:0]), .out(subtractor_2_out[3:0]), .bout(subtractor_2_out[4]));  // open: bin
  Subtractor #(.width(4)) subtractor_3 (
    .a(A[3:0]), .b(B[3:0]), .out(subtractor_3_out[3:0]), .bout(subtractor_3_out[4]));  // open: bin
  Subtractor #(.width(4)) subtractor_4 (
    .a(B[3:0]), .b(A[3:0]), .out(subtractor_4_out[3:0]), .bout(subtractor_4_out[4]));  // open: bin
  Multiplexer #(.width(6)) multiplexer_2 (
    .in0({A[4], adder_1_cout[4], adder_1_out}), .in1(multiplexer_6_out), .out(out_3), .sel(xor_2_out));  // open: en
  Multiplexer #(.width(6)) multiplexer_3 (
    .in0({B[4], subtractor_2_out}), .in1({A[4], subtractor_1_out}), .out(multiplexer_3_out),
    .sel(comparator_1_gt));  // open: en
  Multiplexer #(.width(6)) multiplexer_4 (
    .in0({A[4], adder_2_cout[4], adder_2_out}), .in1(multiplexer_7_out), .out(out_4), .sel(xor_3_out));  // open: en
  Multiplexer #(.width(6)) multiplexer_5 (
    .in0(subtractor_4_out), .in1({A[4], subtractor_3_out}), .out(multiplexer_5_out), .sel(comparator_2_gt));  // open: en
  Multiplexer #(.width(6)) multiplexer_6 (
    .in0(multiplexer_3_out), .in1({6{1'b0}}), .out(multiplexer_6_out), .sel(comparator_1_eq));  // open: en
  Multiplexer #(.width(6)) multiplexer_7 (
    .in0(multiplexer_5_out), .in1({6{1'b0}}), .out(multiplexer_7_out), .sel(comparator_2_eq));  // open: en

  // Notes on the sheet:
  //   Multiplicant
  //   Multiplier
  //   OUTPUT OF MULTIPLICATION
  //   OUTPUT OF ADDITION
  //   OUTPUT OF SUBTRACTION
  //   SUBMITTED BY:-
  //   18BCE011
  //   18BCE008
  //   18BCE040
endmodule
